# Fritzing sketch final circuit (saved by Fritzing 0.9.3b)
breadboards: 1

parts:
  Part1 = Arduino Uno (Rev3) - ICSP
  Adafruit_HUZZAH_ESP8266_Breakout1 = Adafruit HUZZAH ESP8266 Breakout [part_number=2471]
  J1 = Infrared Proximity Sensor

nets:
  N1: Part1.A4/SDA, Adafruit_HUZZAH_ESP8266_Breakout1.#2
  N2: Part1.A5/SCL, Adafruit_HUZZAH_ESP8266_Breakout1.#15
  N3: Part1.D2, J1.Vout
  5V: Part1.5V, Adafruit_HUZZAH_ESP8266_Breakout1.VBat, J1.Vcc
  GND: Part1.GND, Adafruit_HUZZAH_ESP8266_Breakout1.GND, J1.GND
